# Fritzing sketch AirLogger (saved by Fritzing 0.9.3b)

parts:
  part = DC-DC 5V step-up [chip_label="DC-DC 5V step-up" part_number="DC-DC step-up converter 5V" package="DIP (Dual Inline) [THT]"]
  part_2 = LIPO-110mAh [part_number="Any Li battery" package=lipo-110]
  part_3 = MicroSD Card Module [part_number="microSD module"]
  part_4 = Arduino Pro Mini (3.3V) [part_number="Arduino Pro Mini ATMega328 3.3V 8MHz"]
  part_5 = double row female pin header, 8 pins [form="♀ (female)" part_number=PMS5003]
  part_6 = Barometric Pressure Sensor - BMP180 Breakout (GY-68) [part_number=BME280]

nets:
  N1: part.IN+, part_2.+
  N2: part.IN-, part_2.-
  GND: part.GND, part_3.GND, part_4.GND, part_5.pin2, part_6.GND
  VCC: part.5V, part_3.VCC, part_4.RAW, part_5.pin1, part_6.VCC
  N3: part_3.MISO, part_4.MISO
  N4: part_3.MOSI, part_4.MOSI
  N5: part_3.SCK, part_4.SCK
  N6: part_3.CS, part_4.D10
  N7: part_4.A4, part_6.SDA
  N8: part_4.A5, part_6.SCL
  N9: part_4.D3, part_5.pin4
  N10: part_4.D2, part_5.pin5

custom parts:
  DC-DC 5V step-up: Повышающий модуль постоянного напряжения
